# Fritzing sketch Árammérő kapcs_schem (saved by Fritzing 0.9.9b)
breadboards: 1

parts:
  Mod1 = Raspberry Pi 4B
  R10 = Resistor [tolerance=±5% power=0.25 resistance=220 package=THT]
  R9 = Resistor [tolerance=±5% power=0.25 resistance=220 package=THT]
  R1 = Resistor [tolerance=±5% power=0.25 resistance=220 package=THT]
  R3 = Resistor [tolerance=±5% power=0.25 resistance=220 package=THT]
  R5 = Resistor [tolerance=±5% power=0.25 resistance=220 package=THT]
  R4 = Resistor [tolerance=±5% power=0.25 resistance=220 package=THT]
  R6_Védő_ellenállás = Resistor [tolerance=±5% power=0.25 resistance=220 package=THT]
  I(piros) = LED - 5mm [color="Red (633nm)" current=0.030 package="5 mm [THT]"]
  U(zöld) = LED - 5mm [color="Red (633nm)" current=0.030 package="5 mm [THT]"]
  P(kék) = LED - 5mm [color="Red (633nm)" current=0.030 package="5 mm [THT]"]
  R(sárga) = LED - 5mm [color="Red (633nm)" package="5 mm [THT]"]
  INA1 = INA219 DC Current Sensor Breakout
  7SEG1 = 7-Segment LED I2C Backpack (blue)
  R11_mért_ellenállás = Slide Potentiometer [maximum_resistance=10kΩ]
  S1 = Pushbutton [package="[SMD]"]

nets:
  N1: Mod1.3V3, R9.Pin_1
  5V: Mod1.5V, R6_Védő_ellenállás.Pin_1, INA1.VCC, 7SEG1.V+
  N2: Mod1.GPIO2, INA1.SDA, 7SEG1.SDA
  N3: Mod1.GPIO3, INA1.SCL, 7SEG1.SCL
  N4: Mod1.GPIO14, R10.Pin_0
  N5: Mod1.GPIO25, R(sárga).anode
  N6: Mod1.GPIO8, P(kék).anode
  N7: Mod1.GPIO7, U(zöld).anode
  N8: Mod1.ID_SC, I(piros).anode
  GND: Mod1.GND, R1.Pin_0, R3.Pin_0, R5.Pin_0, R4.Pin_0, INA1.GND, 7SEG1.GND, R11_mért_ellenállás.leg1, R11_mért_ellenállás.wiper
  N9: R10.Pin_1, R9.Pin_0, S1.Pin_1
  N10: R1.Pin_1, I(piros).cathode
  N11: R3.Pin_1, U(zöld).cathode
  N12: R5.Pin_1, P(kék).cathode
  N13: R4.Pin_1, R(sárga).cathode
  N14: R6_Védő_ellenállás.Pin_0, INA1.Vin+
  N15: INA1.Vin-, R11_mért_ellenállás.leg2
  GND_2: S1.Pin_4

custom parts:
  INA219 DC Current Sensor Breakout: INA DC Current Sensor Breakout
  7-Segment LED I2C Backpack (blue): 4-digit, 7-segment LED Display with I2C Control
